// Logisim project CPU.circ as structural Verilog: 10 circuits, main circuit main
module main (
);

  wire cpu_1_clk, undriven;
  wire [7:0] cpu_1_data;

  CPU cpu_1 (.RST(undriven), .CLK(cpu_1_clk), .DATA(cpu_1_data));  // open: out_4, out_5, out_6
endmodule

module ALU (
  input  CLK,
  input  WA,
  input  [7:0] A,
  input  WB,
  input  [7:0] B,
  input  WM,
  input  [7:0] Mode,
  output Ready,
  output [7:0] C,
  output [7:0] D
);

  wire d_ff_1_qn;
  wire [0:0] adder_1_cout, subtractor_1_bout;
  wire [1:0] bit_extender_1_out, register_3_q;
  wire [7:0] adder_1_out, multiplier_1_cout, multiplier_1_out, register_1_q, register_2_q, subtractor_1_out;

  Bit_Extender #(.out_width(2)) bit_extender_1 (.in(Mode), .out(bit_extender_1_out));
  Register register_1 (.D(A), .en(WA), .Q(register_1_q), .clk(CLK));  // open: clr
  Register register_2 (.D(B), .en(WB), .Q(register_2_q), .clk(CLK));  // open: clr
  Register #(.width(2)) register_3 (.D(bit_extender_1_out), .en(WM), .Q(register_3_q), .clk(CLK));  // open: clr
  D_Flip_Flop d_ff_1 (.clk(CLK), .D(d_ff_1_qn), .Q(Ready), .Qn(d_ff_1_qn));  // open: preset, en, reset
  Adder adder_1 (.a(register_1_q), .b(register_2_q), .out(adder_1_out), .cout(adder_1_cout[0]));  // open: cin
  Subtractor subtractor_1 (
    .a(register_1_q), .b(register_2_q), .out(subtractor_1_out), .bout(subtractor_1_bout[0]));  // open: bin
  Multiplier multiplier_1 (
    .a(register_1_q), .b(register_2_q), .out(multiplier_1_out), .cout(multiplier_1_cout));  // open: cin
  Multiplexer #(.select(2), .width(8)) multiplexer_1 (
    .in0(adder_1_out), .in1(subtractor_1_out), .in2(multiplier_1_out), .out(C), .sel(register_3_q));  // open: in3, en
  Multiplexer #(.select(2), .width(8)) multiplexer_2 (
    .in0({{7{1'b0}}, adder_1_cout[0]}), .in1({{7{1'b0}}, subtractor_1_bout[0]}), .in2(multiplier_1_cout),
    .out(D), .sel(register_3_q));  // open: in3, en
endmodule

module State_Machine (
  input  RESET,
  input  CLK,
  output [3:0] out_3,
  output out_4,
  output out_5,
  output out_6,
  output out_7,
  output out_8,
  output out_9,
  output out_10,
  output out_11,
  output out_12,
  output out_13,
  output out_14,
  output out_15,
  output out_16,
  output out_17,
  output out_18,
  output out_19
);

  Demultiplexer #(.select(4)) demultiplexer_1 (
    .out0(out_4), .out1(out_5), .out2(out_6), .out3(out_7), .out4(out_8), .out5(out_9), .out6(out_10),
    .out7(out_11), .out8(out_12), .out9(out_13), .out10(out_14), .out11(out_15), .out12(out_16),
    .out13(out_17), .out14(out_18), .out15(out_19), .in(1'b1), .sel(out_3));  // open: en
  Counter #(.width(4), .max('hf), .trigger("falling")) counter_1 (
    .Q(out_3), .clk(CLK), .clr(RESET));  // open: load, D, count, carry
endmodule

module ID (
  input  [7:0] INSTR,
  output [3:0] Immediate,
  output [1:0] RegB,
  output [1:0] RegA,
  output [1:0] Operator,
  output [1:0] Opcode
);


  assign Immediate = INSTR[3:0];
  assign Opcode = INSTR[7:6];
  assign Operator = INSTR[5:4];
  assign RegA = INSTR[3:2];
  assign RegB = INSTR[1:0];
endmodule

module State_Decider (
  input  [3:0] in_1,
  input  in_2,
  input  in_3,
  input  in_4,
  input  in_5,
  input  in_6,
  input  in_7,
  input  in_8,
  input  in_9,
  input  in_10,
  input  in_11,
  input  in_12,
  input  in_13,
  input  in_14,
  input  in_15,
  input  in_16,
  input  in_17,
  input  [3:0] in_18,
  input  [1:0] in_19,
  input  [1:0] in_20,
  input  [1:0] in_21,
  input  [1:0] in_22,
  output [3:0] IMMEDIATE,
  output Increment_PC,
  output Out_RegSelA,
  output Out_RegSelectB,
  output Out_ACC,
  output In_A,
  output In_B,
  output Out__ALU,
  output Out_Immediate,
  output Out_PC,
  output In_IR,
  output In_Reg,
  output Out_Reg,
  output In_ACC,
  output In_Mem_ADDR,
  output In_Mem_DATA,
  output Out_Mem_DATA,
  output In_Mode,
  output Reset_State,
  output [1:0] Mode,
  output Out_Mode,
  output In_RegADDR,
  output [2:0] RegSelectA,
  output [2:0] RegSelectB
);

  wire or_1_out, split_1_out_2, split_1_out_3, split_1_out_4, split_1_out_5, split_1_out_6, split_1_out_7;

  Split split_1 (
    .in_1({in_22, in_21}), .out_2(split_1_out_2), .out_3(split_1_out_3), .out_4(split_1_out_4),
    .out_5(split_1_out_5), .out_6(split_1_out_6), .out_7(split_1_out_7));  // open: out_8, out_9, out_10, out_11, out_12, out_13, out_14, out_15, out_16, out_17
  or or_1 (or_1_out, split_1_out_5, split_1_out_4, split_1_out_3, split_1_out_2);
  assign In_Mode = split_1_out_6 ? in_8 : 1'bz;  // Controlled_Buffer controlled_buffer_1
  assign In_ACC = split_1_out_6 ? in_9 : 1'bz;  // Controlled_Buffer controlled_buffer_2
  assign Reset_State = or_1_out ? in_6 : 1'bz;  // Controlled_Buffer controlled_buffer_3
  assign In_A = split_1_out_6 ? in_6 : 1'bz;  // Controlled_Buffer controlled_buffer_4
  assign In_B = split_1_out_6 ? in_7 : 1'bz;  // Controlled_Buffer controlled_buffer_5
  assign In_B = split_1_out_7 ? in_7 : 1'bz;  // Controlled_Buffer controlled_buffer_6
  assign In_RegADDR = split_1_out_7 ? in_6 : 1'bz;  // Controlled_Buffer controlled_buffer_7
  Pull_Resistor pull_resistor_1 (.node(In_A));
  Pull_Resistor pull_resistor_2 (.node(In_B));
  Pull_Resistor pull_resistor_3 (.node(In_Mode));
  Pull_Resistor pull_resistor_4 (.node(In_ACC));
  Pull_Resistor pull_resistor_5 (.node(In_RegADDR));
  Pull_Resistor pull_resistor_6 (.node(In_B));

  assign IMMEDIATE = in_18;
  assign In_IR = in_4;
  assign In_Mem_ADDR = in_3;
  assign Increment_PC = in_2;
  assign Mode = {1'b0, in_21[1]};
  assign Out__ALU = In_ACC;
  assign Out_ACC = In_A;
  assign Out_Immediate = In_B;
  assign Out_Mem_DATA = in_4;
  assign Out_Mode = In_Mode;
  assign Out_PC = in_3;
  assign Out_Reg = In_B;
  assign Out_RegSelA = In_RegADDR;
endmodule

module PC (
  input  CLK,
  input  [7:0] D,
  input  INCR,
  input  RSTR,
  output [7:0] out_5
);

  wire not_1_out;
  wire [7:0] PC_q;

  not not_1 (not_1_out, INCR);
  assign out_5 = CLK ? PC_q : 8'bz;  // Controlled_Buffer controlled_buffer_1
  Counter PC (.load(INCR), .D(D), .count(not_1_out), .Q(PC_q), .clk(CLK), .clr(RSTR));  // open: carry
endmodule

module Split (
  input  [3:0] in_1,
  output out_2,
  output out_3,
  output out_4,
  output out_5,
  output out_6,
  output out_7,
  output out_8,
  output out_9,
  output out_10,
  output out_11,
  output out_12,
  output out_13,
  output out_14,
  output out_15,
  output out_16,
  output out_17
);

  and and_1 (out_3, ~in_1[3], ~in_1[2], ~in_1[1], in_1[0]);  // AND_Gate
  and and_2 (out_2, ~in_1[3], ~in_1[2], ~in_1[1], ~in_1[0]);  // AND_Gate
  and and_3 (out_4, ~in_1[3], ~in_1[2], in_1[1], ~in_1[0]);  // AND_Gate
  and and_4 (out_5, ~in_1[3], ~in_1[2], in_1[1], in_1[0]);  // AND_Gate
  and and_5 (out_6, ~in_1[3], in_1[2], ~in_1[1], ~in_1[0]);  // AND_Gate
  and and_6 (out_7, ~in_1[3], in_1[2], ~in_1[1], in_1[0]);  // AND_Gate
  and and_7 (out_8, ~in_1[3], in_1[2], in_1[1], ~in_1[0]);  // AND_Gate
  and and_8 (out_9, ~in_1[3], in_1[2], in_1[1], in_1[0]);  // AND_Gate
  and and_9 (out_10, in_1[3], ~in_1[2], ~in_1[1], ~in_1[0]);  // AND_Gate
  and and_10 (out_11, in_1[3], ~in_1[2], ~in_1[1], in_1[0]);  // AND_Gate
  and and_11 (out_12, in_1[3], ~in_1[2], in_1[1], ~in_1[0]);  // AND_Gate
  and and_12 (out_14, in_1[3], in_1[2], ~in_1[1], ~in_1[0]);  // AND_Gate
  and and_13 (out_13, in_1[3], ~in_1[2], in_1[1], in_1[0]);  // AND_Gate
  and and_14 (out_15, in_1[3], in_1[2], ~in_1[1], in_1[0]);  // AND_Gate
  and and_15 (out_17, in_1[3], in_1[2], in_1[1], in_1[0]);
  and and_16 (out_16, in_1[3], in_1[2], in_1[1], ~in_1[0]);  // AND_Gate
endmodule

module CPU (
  input  RST,
  output CLK,
  output [7:0] DATA,
  output [7:0] out_4,
  output [7:0] out_5,
  output [7:0] out_6
);

  wire controlled_buffer_2_out, controlled_buffer_13_out, microcode_1__1_reset_state,
       microcode_1__2_in_alu_a, microcode_1__3_in_alu_b, microcode_1__4_in_alu_mode, microcode_1__5_out_alu,
       microcode_1__6_out_control_immediate, microcode_1__7_out_control_rega,
       microcode_1__8_out_control_regb, microcode_1__9_out_control_mode, microcode_1__10_unused,
       microcode_1__11out_control_0, microcode_1__12_in_reg_ref, microcode_1__13_in_reg_data__only_after_rf,
       microcode_1__14_out_reg_data, microcode_1_in_ir, microcode_1_in_mem_addr, microcode_1_increment_pc,
       microcode_1_out_mem_data, microcode_1_out_pc, or_1_out, state_machine_1_out_4, state_machine_1_out_5,
       state_machine_1_out_6, state_machine_1_out_7, state_machine_1_out_8, state_machine_1_out_9,
       state_machine_1_out_10, state_machine_1_out_11, state_machine_1_out_12, state_machine_1_out_13,
       state_machine_1_out_14, state_machine_1_out_15, state_machine_1_out_16, state_machine_1_out_17,
       state_machine_1_out_18, state_machine_1_out_19, undriven_2;
  wire [1:0] id_1_opcode, id_1_operator, id_1_rega, id_1_regb;
  wire [3:0] id_1_immediate, state_machine_1_out_3;
  wire [7:0] controlled_buffer_1_out, controlled_buffer_4_out, controlled_buffer_5_out,
       controlled_buffer_7_out, controlled_buffer_8_out, controlled_buffer_9_out, controlled_buffer_12_out,
       controlled_buffer_14_out, IR_q, pc_1_out_5, pull_resistor_1_node, ram_1_data, undriven;

  or or_1 (or_1_out, RST, microcode_1__1_reset_state);
  State_Machine state_machine_1 (
    .RESET(or_1_out), .CLK(CLK), .out_3(state_machine_1_out_3), .out_4(state_machine_1_out_4),
    .out_5(state_machine_1_out_5), .out_6(state_machine_1_out_6), .out_7(state_machine_1_out_7),
    .out_8(state_machine_1_out_8), .out_9(state_machine_1_out_9), .out_10(state_machine_1_out_10),
    .out_11(state_machine_1_out_11), .out_12(state_machine_1_out_12), .out_13(state_machine_1_out_13),
    .out_14(state_machine_1_out_14), .out_15(state_machine_1_out_15), .out_16(state_machine_1_out_16),
    .out_17(state_machine_1_out_17), .out_18(state_machine_1_out_18), .out_19(state_machine_1_out_19));
  Clock clock_1 (.out(CLK));
  ID id_1 (
    .INSTR(IR_q), .Immediate(id_1_immediate), .RegB(id_1_regb), .RegA(id_1_rega), .Operator(id_1_operator),
    .Opcode(id_1_opcode));
  Microcode microcode_1 (
    .in_1(state_machine_1_out_3), .in_2(state_machine_1_out_4), .in_3(state_machine_1_out_5),
    .in_4(state_machine_1_out_6), .in_5(state_machine_1_out_7), .in_6(state_machine_1_out_8),
    .in_7(state_machine_1_out_9), .in_8(state_machine_1_out_10), .in_9(state_machine_1_out_11),
    .in_10(state_machine_1_out_12), .in_11(state_machine_1_out_13), .in_12(state_machine_1_out_14),
    .in_13(state_machine_1_out_15), .in_14(state_machine_1_out_16), .in_15(state_machine_1_out_17),
    .in_16(state_machine_1_out_18), .in_17(state_machine_1_out_19), .in_18(id_1_immediate),
    .in_19(id_1_regb), .in_20(id_1_rega), .in_21(id_1_operator), .in_22(id_1_opcode), .IMMEDIATE(DATA),
    .REGA(DATA), .REGB(DATA), .MODE(DATA), ._0(DATA), .Increment_PC(microcode_1_increment_pc),
    .Out_PC(microcode_1_out_pc), .Out_Mem_DATA(microcode_1_out_mem_data), .In_IR(microcode_1_in_ir),
    .In_Mem_ADDR(microcode_1_in_mem_addr), ._1_Reset_State(microcode_1__1_reset_state),
    ._2_In_ALU_A(microcode_1__2_in_alu_a), ._3_In_ALU_B(microcode_1__3_in_alu_b),
    ._4_In_ALU_Mode(microcode_1__4_in_alu_mode), ._5_Out_ALU(microcode_1__5_out_alu),
    ._6_Out_Control_Immediate(microcode_1__6_out_control_immediate),
    ._7_Out_Control_RegA(microcode_1__7_out_control_rega),
    ._8_Out_Control_RegB(microcode_1__8_out_control_regb),
    ._9_Out_Control_Mode(microcode_1__9_out_control_mode), ._10_UNUSED(microcode_1__10_unused),
    ._11Out_Control_0(microcode_1__11out_control_0), ._12_In_Reg_Ref(microcode_1__12_in_reg_ref),
    ._13_In_Reg_Data__ONLY_AFTER_RF(microcode_1__13_in_reg_data__only_after_rf),
    ._14_Out_Reg_Data(microcode_1__14_out_reg_data));  // open: out_47, out_48
  assign controlled_buffer_1_out = microcode_1_in_ir ? DATA : 8'bz;  // Controlled_Buffer controlled_buffer_1
  Register IR (.D(controlled_buffer_1_out), .Q(IR_q), .clk(controlled_buffer_2_out));  // open: en, clr
  assign controlled_buffer_2_out = microcode_1_in_ir ? CLK : 1'bz;  // Controlled_Buffer controlled_buffer_2
  assign DATA = microcode_1_out_pc ? pc_1_out_5 : 8'bz;  // Controlled_Buffer controlled_buffer_3
  PC pc_1 (.CLK(microcode_1_increment_pc), .D(undriven), .RSTR(RST), .out_5(pc_1_out_5));  // open: INCR
  assign controlled_buffer_4_out = microcode_1_in_mem_addr ? DATA : 8'bz;  // Controlled_Buffer controlled_buffer_4
  assign controlled_buffer_5_out = undriven_2 ? DATA : 8'bz;  // Controlled_Buffer controlled_buffer_5
  RAM #(.bus("separate")) ram_1 (
    .addr(controlled_buffer_4_out), .din(controlled_buffer_5_out), .data(ram_1_data), .clk(CLK));  // open: str, sel, ld, clr
  assign DATA = microcode_1_out_mem_data ? ram_1_data : 8'bz;  // Controlled_Buffer controlled_buffer_6
  assign controlled_buffer_7_out = microcode_1__3_in_alu_b ? DATA : 8'bz;  // Controlled_Buffer controlled_buffer_7
  assign controlled_buffer_8_out = microcode_1__2_in_alu_a ? DATA : 8'bz;  // Controlled_Buffer controlled_buffer_8
  assign controlled_buffer_9_out = microcode_1__4_in_alu_mode ? DATA : 8'bz;  // Controlled_Buffer controlled_buffer_9
  ALU alu_1 (
    .CLK(CLK), .WA(microcode_1__2_in_alu_a), .A(controlled_buffer_8_out), .WB(microcode_1__3_in_alu_b),
    .B(controlled_buffer_7_out), .WM(microcode_1__4_in_alu_mode), .Mode(controlled_buffer_9_out), .C(out_4));  // open: Ready, D
  assign DATA = microcode_1__5_out_alu ? out_4 : 8'bz;  // Controlled_Buffer controlled_buffer_10
  assign DATA = microcode_1__14_out_reg_data ? pull_resistor_1_node : 8'bz;  // Controlled_Buffer controlled_buffer_11
  assign controlled_buffer_12_out = microcode_1__13_in_reg_data__only_after_rf ? DATA : 8'bz;  // Controlled_Buffer controlled_buffer_12
  Pull_Resistor pull_resistor_1 (.node(pull_resistor_1_node));
  assign controlled_buffer_13_out = microcode_1__13_in_reg_data__only_after_rf ? CLK : 1'bz;  // Controlled_Buffer controlled_buffer_13
  assign controlled_buffer_14_out = microcode_1__12_in_reg_ref ? DATA : 8'bz;  // Controlled_Buffer controlled_buffer_14
  Register_Array register_array_1 (
    .CLK(CLK), .WRITE(controlled_buffer_13_out), .SetADDR(microcode_1__12_in_reg_ref),
    .Select(controlled_buffer_14_out), .D(controlled_buffer_12_out), .Out(pull_resistor_1_node),
    .out_7(out_5), .out_8(out_6));

  // Notes on the sheet:
  //   PORT CONTROLLER
endmodule

module Register_Array (
  input  [7:0] Select,
  input  [7:0] D,
  input  SetADDR,
  input  CLK,
  input  WRITE,
  output [7:0] Out,
  output [7:0] out_7,
  output [7:0] out_8
);

  wire controlled_buffer_1_out, demultiplexer_1_out0, demultiplexer_1_out1, demultiplexer_1_out2,
       demultiplexer_1_out3, demultiplexer_1_out4, demultiplexer_1_out5, demultiplexer_1_out6,
       demultiplexer_1_out7;
  wire [2:0] bit_extender_1_out, register_1_q;
  wire [7:0] _2_q, _3_q, _4_q, _5_q, _6_q, _7_q;

  assign controlled_buffer_1_out = SetADDR ? CLK : 1'bz;  // Controlled_Buffer controlled_buffer_1
  Pull_Resistor pull_resistor_1 (.node(Select));
  Bit_Extender #(.out_width(3)) bit_extender_1 (.in(Select), .out(bit_extender_1_out));
  Register #(.width(3)) register_1 (
    .D(bit_extender_1_out), .en(controlled_buffer_1_out), .Q(register_1_q), .clk(controlled_buffer_1_out));  // open: clr
  Register ACC (.D(D), .en(demultiplexer_1_out0), .Q(out_7), .clk(WRITE));  // open: clr
  Register _1 (.D(D), .en(demultiplexer_1_out1), .Q(out_8), .clk(WRITE));  // open: clr
  Register _2 (.D(D), .en(demultiplexer_1_out2), .Q(_2_q), .clk(WRITE));  // open: clr
  Register _3 (.D(D), .en(demultiplexer_1_out3), .Q(_3_q), .clk(WRITE));  // open: clr
  Pull_Resistor pull_resistor_2 (.node(Out));
  Multiplexer #(.select(3), .width(8)) multiplexer_1 (
    .in0(out_7), .in1(out_8), .in2(_2_q), .in3(_3_q), .in4(_4_q), .in5(_5_q), .in6(_6_q), .in7(_7_q),
    .out(Out), .sel(register_1_q));  // open: en
  Register _4 (.D(D), .en(demultiplexer_1_out4), .Q(_4_q), .clk(WRITE));  // open: clr
  Demultiplexer #(.select(3)) demultiplexer_1 (
    .out0(demultiplexer_1_out0), .out1(demultiplexer_1_out1), .out2(demultiplexer_1_out2),
    .out3(demultiplexer_1_out3), .out4(demultiplexer_1_out4), .out5(demultiplexer_1_out5),
    .out6(demultiplexer_1_out6), .out7(demultiplexer_1_out7), .in(1'b1), .sel(register_1_q));  // open: en
  Register _5 (.D(D), .en(demultiplexer_1_out5), .Q(_5_q), .clk(WRITE));  // open: clr
  Register _6 (.D(D), .en(demultiplexer_1_out6), .Q(_6_q), .clk(WRITE));  // open: clr
  Register _7 (.D(D), .en(demultiplexer_1_out7), .Q(_7_q), .clk(WRITE));  // open: clr
endmodule

module Microcode (
  input  [3:0] in_1,
  input  in_2,
  input  in_3,
  input  in_4,
  input  in_5,
  input  in_6,
  input  in_7,
  input  in_8,
  input  in_9,
  input  in_10,
  input  in_11,
  input  in_12,
  input  in_13,
  input  in_14,
  input  in_15,
  input  in_16,
  input  in_17,
  input  [3:0] in_18,
  input  [1:0] in_19,
  input  [1:0] in_20,
  input  [1:0] in_21,
  input  [1:0] in_22,
  output Increment_PC,
  output Out_PC,
  output Out_Mem_DATA,
  output In_IR,
  output In_Mem_ADDR,
  output _1_Reset_State,
  output _2_In_ALU_A,
  output _3_In_ALU_B,
  output _4_In_ALU_Mode,
  output _5_Out_ALU,
  output _6_Out_Control_Immediate,
  output _7_Out_Control_RegA,
  output _8_Out_Control_RegB,
  output _9_Out_Control_Mode,
  output _10_UNUSED,
  output _11Out_Control_0,
  output _12_In_Reg_Ref,
  output _13_In_Reg_Data__ONLY_AFTER_RF,
  output [7:0] IMMEDIATE,
  output [7:0] REGA,
  output [7:0] REGB,
  output [7:0] MODE,
  output [7:0] _0,
  output _14_Out_Reg_Data,
  output out_47,
  output out_48
);

  wire [7:0] bit_extender_1_out, bit_extender_2_out, bit_extender_3_out, bit_extender_4_out;

  assign bit_extender_1_out = {{4{1'b0}}, in_18};  // Bit_Extender bit_extender_1
  assign IMMEDIATE = _6_Out_Control_Immediate ? bit_extender_1_out : 8'bz;  // Controlled_Buffer controlled_buffer_1
  assign bit_extender_2_out = {{6{1'b0}}, in_20};  // Bit_Extender bit_extender_2
  assign REGA = _7_Out_Control_RegA ? bit_extender_2_out : 8'bz;  // Controlled_Buffer controlled_buffer_2
  assign bit_extender_3_out = {{6{1'b0}}, in_19};  // Bit_Extender bit_extender_3
  assign REGB = _8_Out_Control_RegB ? bit_extender_3_out : 8'bz;  // Controlled_Buffer controlled_buffer_3
  buf buffer_1 (In_Mem_ADDR, in_3);
  buf buffer_2 (Out_PC, in_3);
  buf buffer_3 (Increment_PC, in_2);
  assign bit_extender_4_out = {{6{1'b0}}, {1'b0, in_21[1]}};  // Bit_Extender bit_extender_4
  assign MODE = _9_Out_Control_Mode ? bit_extender_4_out : 8'bz;  // Controlled_Buffer controlled_buffer_4
  buf buffer_4 (Out_Mem_DATA, in_4);
  buf buffer_5 (In_IR, in_4);
  assign _0 = _11Out_Control_0 ? {8{1'b0}} : 8'bz;  // Controlled_Buffer controlled_buffer_5
  ROM #(.dataWidth(16)) rom_1 (
    .addr({in_22, in_21, in_1}),
    .data({out_48, out_47, _14_Out_Reg_Data, _13_In_Reg_Data__ONLY_AFTER_RF, _12_In_Reg_Ref, _11Out_Control_0, _10_UNUSED, _9_Out_Control_Mode, _8_Out_Control_RegB, _7_Out_Control_RegA, _6_Out_Control_Immediate, _5_Out_ALU, _4_In_ALU_Mode, _3_In_ALU_B, _2_In_ALU_A, _1_Reset_State}));  // open: sel

  // Notes on the sheet:
  //   contents of rom_1 (hex, n*v repeats v):
  //   0 0 0 1 15*0 1 15*0 1 15*0 1 15*0 c00 2002 24 108 1010 11*0 840 2002 c00 2004 108 880 1010 9*0 c00
  //   2002 24 108 1010 11*0 840 2002 c00 2004 108 880 1010
endmodule
